# Fritzing sketch sonyclock (saved by Fritzing 1.0.0rc)

parts:
  J1 = female pin header, 8 pins [form="♀ (female)"]
  On/Off = Pushbutton [package="[THT]"]
  Minute = Pushbutton [package="[THT]"]
  Alarm = Pushbutton [package="[THT]"]
  Hour = Pushbutton [package="[THT]"]
  Time = Pushbutton [package="[THT]"]
  Snooze = Pushbutton [package="[THT]"]
  Part1 = Adafruit MCP9808 [part_number="Adafruit #5027"]
  Part2 = Adafruit I2C+SPI LCD Backpack [part_number="Adafruit #292"]
  MCU1 = Raspberry Pi Zero
  J2 = Piezo Speaker

nets:
  N1: J1.pin1, Minute.Pin_4, MCU1.pin_35
  N2: J1.pin2, Hour.Pin_4, MCU1.pin_37
  GND: J1.pin3, On/Off.Pin_1, On/Off.Pin_2, Minute.Pin_1, Minute.Pin_2, Alarm.Pin_1, Alarm.Pin_2, Hour.Pin_1, Hour.Pin_2, Time.Pin_1, Time.Pin_2, Snooze.Pin_1, Snooze.Pin_2, Part1.GND, Part2.GND, MCU1.pin_9, MCU1.pin_34, MCU1.pin_39, J2.pin1
  N3: J1.pin4, Snooze.Pin_4, MCU1.pin_36
  N4: J1.pin5, Time.Pin_3, Time.Pin_4, MCU1.pin_38
  N5: J1.pin6, Alarm.Pin_3, Alarm.Pin_4, MCU1.pin_40
  N6: J1.pin7, On/Off.Pin_4, MCU1.pin_31
  3.3V: Part1.VCC, Part2.VCC, MCU1.pin_1
  N7: Part1.SDA, Part2.DATA, MCU1.pin_3
  N8: Part1.SCL, Part2.CLOCK, MCU1.pin_5
  N9: MCU1.pin_33, J2.pin2

custom parts:
  Adafruit MCP9808: The MCP9808 digital temperature sensor is one of the more accurate/precise we've ever seen, with a typical accuracy of ±0.25°C over the sensor's -40°C to +125°C range and precision of +0.0625°C. They work great with any microcontroller using standard I2C. With three address jumpers on the back, you can connect up to 8 to a single I2C bus without address collisions. Best of all, a wide voltage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
  Adafruit I2C+SPI LCD Backpack: LCD backpacks reduce the number of pins needed to connect to an LCD. LCDs are a fun and easy way to have your microcontroller project talk back to you. Character LCDs are common, and easy to get, available in tons of colors and sizes. We've written tutorials on using character LCDs with an Arduino (or similar microcontroller) but find that the number of pins necessary to control the LCD can be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
